# Fritzing sketch sPC (saved by Fritzing 0.9.3b)
breadboards: 1

parts:
  YwRobot_Power_Supply1 = YwRobot Breadboard Power Supply [part_number=545043]
  KY-1 = Keyes Relay [package=THT]
  U1 = ESP8266 ESP-01 Upgraded WiFi Module [part_number=ESP8266]
  Part1 = Arduino Uno (Rev3)
  DHT1 = DHT11 Humitidy and Temperature Sensor
  R1 = Resistor [tolerance=±5% resistance=10k package=THT]
  R3 = Resistor [tolerance=±5% resistance=220 package="0603 [SMD]"]

nets (from the breadboard view):
  N1: YwRobot_Power_Supply1.VCC#5, U1.VCC, R3.Pin_0
  N2: YwRobot_Power_Supply1.VCC#9, KY-1.power, DHT1.VDD, R1.Pin_0
  N3: YwRobot_Power_Supply1.GND#11, U1.GND
  GND: YwRobot_Power_Supply1.GND#13, KY-1.ground, Part1.GND, DHT1.GND
  N4: KY-1.signal, Part1.D13/SCK
  N5: U1.RXD, Part1.D2
  N6: U1.CH_PD, R3.Pin_1
  N7: U1.TXD, Part1.D3_PWM
  N8: Part1.D7, DHT1.DATA, R1.Pin_1

custom parts:
  YwRobot Breadboard Power Supply: The YwRobot Breadboard Power Supply (MB-V2) has two power rails; they can be 5V or 3V3. Power to the module can be provided through the female USB socket or through the A10 (female) 2.1mm power jack.
  Keyes Relay: The Keyes 5V relay module is suitable for SCM development, home appliance control. It uses a 5V~12V TIL control signal which can control DC / AC signal.
  ESP8266 ESP-01 Upgraded WiFi Module: Upgraded Version ESP-01,all Flash are upgraded to 1M byte.Also support Cloud service remote transmission.
  DHT11 Humitidy and Temperature Sensor: DHT11 Humidity and Temperature Sensor
